# Fritzing sketch ZS-Brushless (saved by Fritzing 0.9.6b)
circuit board: 4.30719cm x 3.05242cm
breadboards: 1

parts:
  U1 = Sharp PC817 [package=THT]
  U2 = Sharp PC817 [package=THT]
  U3 = Sharp PC817 [package=THT]
  R1 = Resistor [tolerance=±5% resistance=1k package="1206 [SMD]"]
  R2 = Resistor [tolerance=±5% resistance=1k package="1206 [SMD]"]
  R3 = Resistor [tolerance=±5% resistance=100k power=0.25 package=THT]
  PWM = Header 1 [package=1x01_offset]
  Break = Header 1 [package=1x01_offset]
  GND = Header 1 [package=1x01_offset]
  R4 = Resistor [tolerance=±5% resistance=1k package="1206 [SMD]"]
  Break_2 = Header 1 [package=1x01_offset]
  GND_2 = Header 1 [package=1x01_offset]
  HALL = Header 1 [package=1x01_offset]
  HALL_2 = Header 1 [package=1x01_offset]
  3_3V = Header 1 [package=1x01_offset]
  R5 = Resistor [tolerance=±5% resistance=4.7k package="1206 [SMD]"]
  PWM_2 = Header 1 [package=1x01_offset]
  DIR = Header 1 [package=1x01_offset]
  DIR_2 = Header 1 [package=1x01_offset]
  +5V = Header 1 [package=1x01_offset]

nets:
  N1: U1.Pin_1, R4.Pin_0
  N2: U1.Pin_2, U1.Pin_3, U2.Pin_2, U2.Pin_3, U3.Pin_2, U3.Pin_3, R3.Pin_0, R3.Pin_1, Break.1, GND.1, GND_2.1
  N3: U1.Pin_4, HALL.1, R5.Pin_1
  N4: U2.Pin_1, R2.Pin_1
  N5: U2.Pin_4, DIR_2.1
  N6: U3.Pin_1, R1.Pin_1
  N7: U3.Pin_4, +5V.1
  N8: R1.Pin_0, Break_2.1
  N9: R2.Pin_0, DIR.1
  N10: PWM.1, PWM_2.1
  N11: R4.Pin_1, HALL_2.1
  N12: 3_3V.1, R5.Pin_0

notes:
  ZS-X11H Expander
  Rev. 1.1
  (c) USU 2024-02
